// Logisim project s-mips.circ as structural Verilog
module S_MIPS_Board (
  input  DESHABILITAR_DISPATCHER,
  output halt
);

  wire button_1_out, CLK, CS, d_ff_1_q, LCLR, LoadRAM, LoadRAMOn, LW, R_R_W, R_W, ram_dispatcher_1_finished,
       RCS, Reset_out, RST, TTY_EN;
  wire [2:0] KDB;
  wire [3:0] LMask, Mask, ram_1_read_time, ram_1_write_time, RMask;
  wire [6:0] KDB_DATA, TTY_DATA;
  wire [15:0] Addr, LAddr, RAddr;
  wire [31:0] I0, I1, I2, I3, LData, ram_1_data_out_0, ram_1_data_out_1, ram_1_data_out_2, ram_1_data_out_3,
       RI0, RI1, RI2, RI3;

  TTY #(.rows(25), .cols(80)) tty_1 (.data(TTY_DATA), .clk(CLK), .we(TTY_EN), .clr(RST));
  not not_1 (LoadRAMOn, ram_dispatcher_1_finished);
  RAM_Dispatcher ram_dispatcher_1 (
    .WriteTime(ram_1_write_time), .Clock(CLK), .Data(LData), .Address(LAddr), .Mask(LMask),
    .Finished(ram_dispatcher_1_finished), .Write(LW), .CLR(LCLR));
  Keyboard #(.buflen(64)) keyboard_1 (.clk(CLK), .re(KDB[0]), .avail(KDB[2]), .data(KDB_DATA));  // open: clr
  RAM ram_1 (
    .Address(RAddr), .Data_Out_0(ram_1_data_out_0), .Data_Out_1(ram_1_data_out_1),
    .Data_Out_2(ram_1_data_out_2), .Data_Out_3(ram_1_data_out_3), .Data_In_0(RI0), .Data_In_1(RI1),
    .Data_In_2(RI2), .Data_In_3(RI3), .Mask(RMask), .nRead_Write(R_R_W), .Chip_Select(RCS),
    .Read_Time(ram_1_read_time), .Reset(button_1_out), .Write_Time(ram_1_write_time));
  Button button_1 (.out(button_1_out));
  D_Flip_Flop d_ff_1 (.clk(CLK), .D(1'b1), .Q(d_ff_1_q), .reset(Reset_out));  // open: Qn, preset, en
  Button Reset (.out(Reset_out));
  S_MIPS s_mips_1 (
    .Kbd_Enable(KDB[0]), .Address(Addr), .Kbd_Clear(KDB[1]), .Kbd_Available(KDB[2]), .RAM_In_0(I0),
    .Kbd_ASCII_Data(KDB_DATA), .RAM_In_1(I1), .TTY_Enable(TTY_EN), .RAM_In_2(I2), .RAM_In_3(I3),
    .TTY_ASCII_Data(TTY_DATA), .Reset(RST), .RAM_Out_0(ram_1_data_out_0), .Clock(CLK),
    .RAM_Out_1(ram_1_data_out_1), .Stop(halt), .RAM_Out_2(ram_1_data_out_2), .RAM_Out_3(ram_1_data_out_3),
    .Mask(Mask), .Read_Time(ram_1_read_time), .Write_Time(ram_1_write_time), .nRead_Write(R_W),
    .Chip_Select(CS));
  D_Flip_Flop d_ff_2 (.clk(CLK), .D(d_ff_1_q), .Qn(LCLR), .reset(Reset_out));  // open: Q, preset, en
  or or_1 (RST, LCLR, LoadRAM);
  Clock clock_1 (.out(CLK));
  Multiplexer #(.width(32), .enable("false")) multiplexer_1 (.in0(I0), .in1(LData), .out(RI0), .sel(LoadRAM));
  Multiplexer #(.width(32), .enable("false")) multiplexer_2 (.in0(I1), .in1(LData), .out(RI1), .sel(LoadRAM));
  Multiplexer #(.width(32), .enable("false")) multiplexer_3 (.in0(I2), .in1(LData), .out(RI2), .sel(LoadRAM));
  Multiplexer #(.width(32), .enable("false")) multiplexer_4 (.in0(I3), .in1(LData), .out(RI3), .sel(LoadRAM));
  and and_1 (LoadRAM, ~DESHABILITAR_DISPATCHER, LoadRAMOn);  // AND_Gate
  Multiplexer #(.width(16), .enable("false")) multiplexer_5 (.in0(Addr), .in1(LAddr), .out(RAddr), .sel(LoadRAM));
  Multiplexer #(.width(4), .enable("false")) multiplexer_6 (.in0(Mask), .in1(LMask), .out(RMask), .sel(LoadRAM));
  Multiplexer #(.enable("false")) multiplexer_7 (.in0(CS), .in1(LW), .out(RCS), .sel(LoadRAM));
  Multiplexer #(.enable("false")) multiplexer_8 (.in0(R_W), .in1(LW), .out(R_R_W), .sel(LoadRAM));

  // Notes on the sheet:
  //   NO MODIFICAR
  //   Keyboard
endmodule

module RAM (
  input  [15:0] Address,
  input  [31:0] Data_In_0,
  input  [31:0] Data_In_1,
  input  [31:0] Data_In_2,
  input  [31:0] Data_In_3,
  input  [3:0] Mask,
  input  nRead_Write,
  input  Chip_Select,
  input  Reset,
  output [31:0] Data_Out_0,
  output [31:0] Data_Out_1,
  output [31:0] Data_Out_2,
  output [31:0] Data_Out_3,
  output [3:0] Read_Time,
  output [3:0] Write_Time
);

  wire and_2_out, and_3_out, and_4_out, and_5_out, and_6_out, and_7_out, and_8_out, and_9_out, Changed, CLK,
       comparator_2_eq, comparator_3_eq, comparator_4_eq, comparator_5_eq, comparator_6_eq, Count,
       demultiplexer_3_out0, Idle, Idle_q, Load, Load0, Load1, nand_1_out, or_1_out, or_2_out, or_3_out,
       or_4_out, or_5_out, or_6_out, or_7_out, or_8_out, or_9_out, or_10_out, Proc_q, Update_Mem, Zero_Time;
  wire [3:0] counter_1_q, multiplexer_1_out, subtractor_1_out;
  wire [31:0] register_1_q, register_2_q, register_3_q, register_4_q, register_5_q;

  // Probe on 4'b0011
  // Probe on 4'b0010
  Multiplexer #(.width(4), .enable("false")) multiplexer_1 (
    .in0(4'b0011), .in1(4'b0010), .out(multiplexer_1_out), .sel(nRead_Write));
  or or_1 (or_1_out, Idle, Update_Mem);
  or or_2 (or_2_out, ~Chip_Select, Reset);  // OR_Gate
  Subtractor #(.width(4)) subtractor_1 (.a(multiplexer_1_out), .b(4'b0010), .out(subtractor_1_out));  // open: bin, bout
  D_Flip_Flop u_Idle (.clk(CLK), .D(or_1_out), .Q(Idle_q), .preset(or_2_out));  // open: Qn, en, reset
  Demultiplexer #(.enable("false")) demultiplexer_1 (.out0(Idle), .out1(Load0), .in(Idle_q), .sel(Changed));
  // Probe on counter_1_q
  Counter #(.width(4), .max('hf)) counter_1 (
    .load(Load), .D(subtractor_1_out), .count(Count), .Q(counter_1_q), .clk(CLK), .clr(or_3_out));  // open: carry
  or or_3 (or_3_out, ~Chip_Select, Reset);  // OR_Gate
  Comparator #(.width(4), .mode("unsigned")) comparator_1 (
    .a(4'b0000), .b(counter_1_q), .eq(Zero_Time));  // open: gt, lt
  or or_4 (or_4_out, Count, Load0, Load1);
  Register #(.width(32)) register_1 (.D(Data_In_0), .en(Chip_Select), .Q(register_1_q), .clk(CLK), .clr(or_5_out));
  or or_5 (or_5_out, ~Chip_Select, Reset);  // OR_Gate
  Register #(.width(32)) register_2 (.D(Data_In_1), .en(Chip_Select), .Q(register_2_q), .clk(CLK), .clr(or_6_out));
  or or_6 (or_6_out, ~Chip_Select, Reset);  // OR_Gate
  Register #(.width(32)) register_3 (.D(Data_In_2), .en(Chip_Select), .Q(register_3_q), .clk(CLK), .clr(or_7_out));
  or or_7 (or_7_out, ~Chip_Select, Reset);  // OR_Gate
  Register #(.width(32)) register_4 (.D(Data_In_3), .en(Chip_Select), .Q(register_4_q), .clk(CLK), .clr(or_8_out));
  or or_8 (or_8_out, ~Chip_Select, Reset);  // OR_Gate
  Register #(.width(32)) register_5 (
    .D({{11{1'b1}}, nRead_Write, Mask, Address}), .en(Chip_Select), .Q(register_5_q), .clk(CLK),
    .clr(or_9_out));
  or or_9 (or_9_out, ~Chip_Select, Reset);  // OR_Gate
  D_Flip_Flop Proc (.clk(CLK), .D(or_4_out), .Q(Proc_q), .reset(or_10_out));  // open: Qn, preset, en
  or or_10 (or_10_out, ~Chip_Select, Reset);  // OR_Gate
  Demultiplexer #(.enable("false")) demultiplexer_2 (
    .out0(Count), .out1(Update_Mem), .in(demultiplexer_3_out0), .sel(Zero_Time));
  Demultiplexer #(.enable("false")) demultiplexer_3 (
    .out0(demultiplexer_3_out0), .out1(Load1), .in(Proc_q), .sel(Changed));
  Clock clock_1 (.out(CLK));
  Comparator #(.width(32)) comparator_2 (.a(register_1_q), .b(Data_In_0), .eq(comparator_2_eq));  // open: gt, lt
  Comparator #(.width(32)) comparator_3 (.a(register_2_q), .b(Data_In_1), .eq(comparator_3_eq));  // open: gt, lt
  Comparator #(.width(32)) comparator_4 (.a(register_3_q), .b(Data_In_2), .eq(comparator_4_eq));  // open: gt, lt
  Comparator #(.width(32)) comparator_5 (.a(register_4_q), .b(Data_In_3), .eq(comparator_5_eq));  // open: gt, lt
  Comparator #(.width(32)) comparator_6 (
    .a(register_5_q), .b({{11{1'b1}}, nRead_Write, Mask, Address}), .eq(comparator_6_eq));  // open: gt, lt
  nand nand_1 (nand_1_out, comparator_6_eq, comparator_2_eq, comparator_3_eq, comparator_4_eq, comparator_5_eq);
  and and_1 (Changed, nand_1_out, Chip_Select);
  or or_11 (Load, Count, Load1, Load0);
  and and_2 (and_2_out, Mask[0], Update_Mem, nRead_Write);
  and and_3 (and_3_out, Mask[1], Update_Mem, nRead_Write);
  and and_4 (and_4_out, Mask[2], Update_Mem, nRead_Write);
  and and_5 (and_5_out, Mask[3], Update_Mem, nRead_Write);
  RAM_part #(.addrWidth(16), .dataWidth(32), .bus("separate")) ram_1 (
    .addr(Address), .din(Data_In_0), .data(Data_Out_0), .str(and_2_out), .sel(Chip_Select), .clk(CLK),
    .ld(and_6_out), .clr(Reset));
  and and_6 (and_6_out, ~nRead_Write, Idle);  // AND_Gate
  RAM_part #(.addrWidth(16), .dataWidth(32), .bus("separate")) ram_2 (
    .addr(Address), .din(Data_In_1), .data(Data_Out_1), .str(and_3_out), .sel(Chip_Select), .clk(CLK),
    .ld(and_7_out), .clr(Reset));
  and and_7 (and_7_out, ~nRead_Write, Idle);  // AND_Gate
  RAM_part #(.addrWidth(16), .dataWidth(32), .bus("separate")) ram_3 (
    .addr(Address), .din(Data_In_2), .data(Data_Out_2), .str(and_4_out), .sel(Chip_Select), .clk(CLK),
    .ld(and_8_out), .clr(Reset));
  and and_8 (and_8_out, ~nRead_Write, Idle);  // AND_Gate
  RAM_part #(.addrWidth(16), .dataWidth(32), .bus("separate")) ram_4 (
    .addr(Address), .din(Data_In_3), .data(Data_Out_3), .str(and_5_out), .sel(Chip_Select), .clk(CLK),
    .ld(and_9_out), .clr(Reset));
  and and_9 (and_9_out, ~nRead_Write, Idle);  // AND_Gate

  assign Read_Time = 4'b0011;
  assign Write_Time = 4'b0010;

  // Other names for the same wires on the sheet: M0 = Mask[0]; M1 = Mask[1]; M2 = Mask[2]; M3 = Mask[3];
  //   RW = nRead_Write; CLR = Reset; CS = Chip_Select; Load2 = Count

  // Notes on the sheet:
  //   NO MODIFICAR
  //   excepto quizás los valores RT y WT
  //   BANK0
  //   BANK1
  //   BANK2
  //   BANK3
endmodule

module S_MIPS (
  input  Kbd_Available,
  input  [6:0] Kbd_ASCII_Data,
  input  [31:0] RAM_Out_0,
  input  [31:0] RAM_Out_1,
  input  Reset,
  input  [31:0] RAM_Out_2,
  input  Clock,
  input  [31:0] RAM_Out_3,
  input  [3:0] Read_Time,
  input  [3:0] Write_Time,
  output Kbd_Enable,
  output [15:0] Address,
  output Kbd_Clear,
  output TTY_Enable,
  output [6:0] TTY_ASCII_Data,
  output Stop,
  output [31:0] RAM_In_0,
  output [31:0] RAM_In_1,
  output [31:0] RAM_In_2,
  output [31:0] RAM_In_3,
  output [3:0] Mask,
  output nRead_Write,
  output Chip_Select
);

  wire Hi_Lo_Op, Inme_Op, KBD_Data_Path, Load_Inst, Load_PC, Logic_Inme_Op, lw, mfhi_Op, Mul_Div_Op, pop,
       RAM_OP, Random, RW_RF, Sign_Op, SP, Stack_Op;
  wire [1:0] offset;
  wire [2:0] Branch_Selector;
  wire [3:0] ALU_Selector;
  wire [5:0] Func_Code, Op_Code;
  wire [31:0] KBD_Data_1, To_RAM, undriven;

  assign KBD_Data_1 = {{25{1'b0}}, Kbd_ASCII_Data};  // Bit_Extender bit_extender_1
  Multiplexer #(.width(32), .enable("false")) multiplexer_1 (
    .in0({32{1'b1}}), .in1(KBD_Data_1), .sel(Kbd_Available));  // open: out
  DataPath datapath_1 (
    .Bank_0(RAM_Out_0), .Bank_1(RAM_Out_1), .Bank_2(RAM_Out_2), .Bank_3(RAM_Out_3), .KBD_Data(undriven),
    .Alu_Op(ALU_Selector), .Branch_Op(Branch_Selector), .Clk(Clock), .Reset(Reset), .Load_PC(Load_PC),
    .Load_Inst(Load_Inst), .R___W(RW_RF), .Inme_Op(Inme_Op), .Logical_Inme_Op(Logic_Inme_Op),
    .Hi_Lo_Register_Op(Hi_Lo_Op), .mfhi(mfhi_Op), .Ram_Op(RAM_OP), .lw(lw), .Stack_Op(Stack_Op), .pop(pop),
    .Load_SP(SP), .Hi_Selector(Mul_Div_Op), .Signed_Op(Sign_Op), .KBD(KBD_Data_Path), .Random(Random),
    .To_Ram(To_RAM), .Adress(Address), .Op_Code(Op_Code), .Func_Code(Func_Code), .tty(TTY_ASCII_Data),
    .offset(offset), .Mask(Mask));
  Control_Unit_2 control_unit_1 (
    .Op_code(Op_Code), .Func_code(Func_Code), .Read_Time(Read_Time), .Write_Time(Write_Time), .Clk(Clock),
    .Reset(Reset), .End_Program(Stop), .Alu(ALU_Selector), .Branch(Branch_Selector), .Sign(Sign_Op),
    .MFHI(mfhi_Op), .Logic(Logic_Inme_Op), .Mul_Div(Mul_Div_Op), .Inmediate(Inme_Op), .Hi_Lo(Hi_Lo_Op),
    .Output(Random), .KBD_DP(KBD_Data_Path), .S_lw(lw), .Stack_Op(Stack_Op), .S_pop(pop), .SP(SP),
    .R_W_RAM(nRead_Write), .Load_PC(Load_PC), .Load_Inst(Load_Inst), .R_W(RW_RF), .RAM_Op(RAM_OP),
    .CS(Chip_Select), .KBD_Enable(Kbd_Enable), .TTY_Enable(TTY_Enable));
  Demultiplexer #(.select(2), .width(32), .enable("false")) demultiplexer_1 (
    .out0(RAM_In_0), .out1(RAM_In_1), .out2(RAM_In_2), .out3(RAM_In_3), .in(To_RAM), .sel(offset));

  assign Kbd_Clear = Reset;

  // Other names for the same wires on the sheet: CLK = Clock; CS = Chip_Select; KBD_AVAIL = Kbd_Available;
  //   CLR = Reset; KBD_CLR = Reset; KBD_DATA[6:0] = Kbd_ASCII_Data; RAM_A[15:0] = Address;
  //   RAM_INPUT_0[31:0] = RAM_In_0; RAM_INPUT_1[31:0] = RAM_In_1; RAM_INPUT_2[31:0] = RAM_In_2;
  //   RAM_INPUT_3[31:0] = RAM_In_3; RAM_MASK[3:0] = Mask; RAM_OUTPUT_0[31:0] = RAM_Out_0;
  //   RAM_OUTPUT_1[31:0] = RAM_Out_1; RAM_OUTPUT_2[31:0] = RAM_Out_2; RAM_OUTPUT_3[31:0] = RAM_Out_3;
  //   RW = nRead_Write; RW_Ram = nRead_Write; TTY_DATA[6:0] = TTY_ASCII_Data

  // Notes on the sheet:
  //   RAM ADDRESS
  //   DATA FROM RAM
  //   DATA TO RAM
  //   DATA WRITE MASK
  //   RAM TIMING
  //   RAM CONTROL
  //   KEYBOARD
  //   TTY
  //   SEQUENCING
endmodule

module RAM_Dispatcher (
  input  [3:0] WriteTime,
  input  Clock,
  input  CLR,
  output [31:0] Data,
  output [15:0] Address,
  output [3:0] Mask,
  output Finished,
  output Write
);

  wire demultiplexer_2_out1, demultiplexer_3_out1, End, IDLE_q, IncAddr, Load, or_1_out, or_2_out, While_q,
       WriteEnd;
  wire [3:0] counter_1_q;
  wire [31:0] CurrentAddress_q;

  Counter #(.width(32), .max('hffffffff)) CurrentAddress (
    .count(IncAddr), .Q({CurrentAddress_q[31:18], Address, CurrentAddress_q[1:0]}), .clk(Clock), .clr(CLR));  // open: load, D, carry
  or or_1 (or_1_out, IncAddr, demultiplexer_3_out1, Finished);
  D_Flip_Flop IDLE (.clk(Clock), .D(or_1_out), .Q(IDLE_q), .preset(CLR));  // open: Qn, en, reset
  Demultiplexer #(.enable("false")) demultiplexer_1 (.out0(Load), .out1(Finished), .in(IDLE_q), .sel(End));
  D_Flip_Flop While (.clk(Clock), .D(or_2_out), .Q(While_q), .reset(CLR));  // open: Qn, preset, en
  or or_2 (or_2_out, Write, Load);
  RAM_part #(.addrWidth(18), .dataWidth(32)) ram_1 (
    .addr({Address, CurrentAddress_q[1:0]}), .data(Data), .clk(Clock));  // open: sel, ld, clr
  Demultiplexer #(.enable("false")) demultiplexer_2 (
    .out0(Write), .out1(demultiplexer_2_out1), .in(While_q), .sel(WriteEnd));
  Decoder #(.select(2)) decoder_1 (
    .out0(Mask[0]), .out1(Mask[1]), .out2(Mask[2]), .out3(Mask[3]), .sel(CurrentAddress_q[1:0]));  // open: en
  Demultiplexer #(.enable("false")) demultiplexer_3 (
    .out0(IncAddr), .out1(demultiplexer_3_out1), .in(demultiplexer_2_out1), .sel(End));
  Counter #(.width(4), .max('hf)) counter_1 (
    .load(Load), .D(WriteTime), .count(Write), .Q(counter_1_q), .clk(Clock));  // open: carry, clr
  Comparator #(.width(32)) comparator_1 (.a(Data), .b({32{1'b1}}), .eq(End));  // open: gt, lt
  Comparator #(.width(4)) comparator_2 (.a(4'b0000), .b(counter_1_q), .eq(WriteEnd));  // open: gt, lt

  // Other names for the same wires on the sheet: CLK = Clock; Count = Write; WT[3:0] = WriteTime
endmodule

module ALU_2 (
  input  [31:0] Rs,
  input  [31:0] Rt,
  input  [3:0] in_3,
  input  Hi_Selector,
  input  Signed_Op,
  output [31:0] Output__Lo,
  output [31:0] Hi,
  output Cero,
  output Negative,
  output Great,
  output Equal,
  output Less
);

  wire comparator_1_lt, comparator_2_lt;
  wire [31:0] Add, And, Hi_Mul_Signed, Hi_Mul_Unsigned, Lo_Div_Signed, Lo_Div_Unsigned, Lo_Mul_Signed,
       Lo_Mul_Unsigned, multiplexer_3_out, multiplexer_4_out, Nor, Or, Remainder_Signed, Remainder_Unsigned,
       slt, sltu, Sub, Xor;

  assign And = Rs & Rt;  // AND_Gate and_1, 32 bits wide
  assign Xor = Rs ^ Rt;  // XOR_Gate xor_1, 32 bits wide
  Comparator #(.width(32)) comparator_1 (.a(Rs), .b(Rt), .lt(comparator_1_lt));  // open: gt, eq
  Multiplier #(.width(32)) multiplier_1 (.a(Rs), .b(Rt), .out(Lo_Mul_Unsigned), .cout(Hi_Mul_Unsigned));  // open: cin
  Divider #(.width(32)) divider_1 (.a(Rs), .b(Rt), .out(Lo_Div_Unsigned), .rem(Remainder_Unsigned));  // open: upper
  Multiplexer #(.width(32), .enable("false")) multiplexer_1 (
    .in0({32{1'b0}}), .in1(32'h1), .out(slt), .sel(comparator_1_lt));
  assign Or = Rs | Rt;  // OR_Gate or_1, 32 bits wide
  Adder #(.width(32)) adder_1 (.a(Rs), .b(Rt), .out(Add));  // open: cin, cout
  assign Nor = ~(Rs | Rt);  // NOR_Gate nor_1, 32 bits wide
  Subtractor #(.width(32)) subtractor_1 (.a(Rs), .b(Rt), .out(Sub));  // open: bin, bout
  Signed_Multiplier signed_multiplier_1 (.A(Rs), .B(Rt), .Lo_Signed(Lo_Mul_Signed), .Hi_Signed(Hi_Mul_Signed));
  Signer_Divider signer_divider_1 (.A(Rs), .B(Rt), .Lo_Div_Sign(Lo_Div_Signed), .Remainder_Sign(Remainder_Signed));
  Comparator #(.width(32), .mode("unsigned")) comparator_2 (.a(Rs), .b(Rt), .lt(comparator_2_lt));  // open: gt, eq
  Multiplexer #(.width(32), .enable("false")) multiplexer_2 (
    .in0({32{1'b0}}), .in1(32'h1), .out(sltu), .sel(comparator_2_lt));
  Multiplexer #(.width(32), .enable("false")) multiplexer_3 (
    .in0(Hi_Mul_Unsigned), .in1(Hi_Mul_Signed), .out(multiplexer_3_out), .sel(Signed_Op));
  Multiplexer #(.width(32), .enable("false")) multiplexer_4 (
    .in0(Remainder_Unsigned), .in1(Remainder_Signed), .out(multiplexer_4_out), .sel(Signed_Op));
  Multiplexer #(.width(32), .enable("false")) multiplexer_5 (
    .in0(multiplexer_3_out), .in1(multiplexer_4_out), .out(Hi), .sel(Hi_Selector));
  Comparator #(.width(32)) comparator_3 (.a(Output__Lo), .b({32{1'b0}}), .eq(Cero), .lt(Negative));  // open: gt
  Multiplexer #(.select(4), .width(32), .enable("false")) multiplexer_6 (
    .in0(Add), .in1(Sub), .in2(Lo_Mul_Signed), .in3(Lo_Mul_Unsigned), .in4(Lo_Div_Unsigned),
    .in5(Lo_Div_Signed), .in6(And), .in7(Or), .in8(Nor), .in9(Xor), .in10(slt), .in11(sltu),
    .out(Output__Lo), .sel(in_3));  // open: in12, in13, in14, in15
  Comparator #(.width(32)) comparator_4 (.a(Rs), .b(Rt), .gt(Great), .eq(Equal), .lt(Less));

  // Other names for the same wires on the sheet: A[31:0] = Rs; B[31:0] = Rt; Result[31:0] = Output__Lo;
  //   Selector[3:0] = in_3
endmodule

module Complemento_A2 (
  input  [31:0] A,
  output [31:0] out_2
);

  wire [31:0] Negated_A;

  // Probe on A
  assign Negated_A = ~A;  // NOT_Gate not_1, 32 bits wide
  Adder #(.width(32)) adder_1 (.a(Negated_A), .b(32'h1), .out(out_2));  // open: cin, cout
  // Probe on out_2
endmodule

// Data B
module Signed_Multiplier (
  input  [31:0] A,
  input  [31:0] B,
  output [31:0] Lo_Signed,
  output [31:0] Hi_Signed
);

  wire adder_1_cout, Sign_Result;
  wire [31:0] A_Complement, B_Complement, Hi_A___B, Hi_A___B_Complement, Hi_A_Complement___B_Complement,
       Hi_A_Complement__B, Hi_Complement, Hi_Result, Lo_A___B, Lo_A___B_Complement, Lo_A_Complement___B,
       Lo_A_Complement___B_Complement, Lo_Complement, Lo_Result, not_1_out, not_2_out;

  // Probe on A
  // Probe on B
  xor xor_1 (Sign_Result, A[31], B[31]);
  Multiplier #(.width(32)) multiplier_1 (.a(A), .b(B), .out(Lo_A___B), .cout(Hi_A___B));  // open: cin
  // Probe on {A[31], B[31]}
  // Probe on Lo_A___B
  // Probe on Hi_A___B
  Multiplier #(.width(32)) multiplier_2 (
    .a(A_Complement), .b(B), .out(Lo_A_Complement___B), .cout(Hi_A_Complement__B));  // open: cin
  Multiplier #(.width(32)) multiplier_3 (
    .a(A), .b(B_Complement), .out(Lo_A___B_Complement), .cout(Hi_A___B_Complement));  // open: cin
  Multiplier #(.width(32)) multiplier_4 (
    .a(A_Complement), .b(B_Complement), .out(Lo_A_Complement___B_Complement),
    .cout(Hi_A_Complement___B_Complement));  // open: cin
  Complemento_A2 complemento_a2_1 (.A(B), .out_2(B_Complement));
  Complemento_A2 complemento_a2_2 (.A(A), .out_2(A_Complement));
  // Probe on B_Complement
  // Probe on Lo_Result
  Multiplexer #(.select(2), .width(32), .enable("false")) multiplexer_1 (
    .in0(Lo_A___B), .in1(Lo_A___B_Complement), .in2(Lo_A_Complement___B),
    .in3(Lo_A_Complement___B_Complement), .out(Lo_Result), .sel({A[31], B[31]}));
  assign not_1_out = ~Lo_Result;  // NOT_Gate not_1, 32 bits wide
  assign not_2_out = ~Hi_Result;  // NOT_Gate not_2, 32 bits wide
  Multiplexer #(.select(2), .width(32), .enable("false")) multiplexer_2 (
    .in0(Hi_A___B), .in1(Hi_A___B_Complement), .in2(Hi_A_Complement__B),
    .in3(Hi_A_Complement___B_Complement), .out(Hi_Result), .sel({A[31], B[31]}));
  Adder #(.width(32)) adder_1 (.a(not_1_out), .b(32'h1), .out(Lo_Complement), .cout(adder_1_cout));  // open: cin
  // Probe on Hi_Result
  Adder #(.width(32)) adder_2 (.a(not_2_out), .b(32'h1), .out(Hi_Complement), .cin(adder_1_cout));  // open: cout
  // Probe on Lo_Signed
  Multiplexer #(.width(32), .enable("false")) multiplexer_3 (
    .in0(Lo_Result), .in1(Lo_Complement), .out(Lo_Signed), .sel(Sign_Result));
  Multiplexer #(.width(32), .enable("false")) multiplexer_4 (
    .in0(Hi_Result), .in1(Hi_Complement), .out(Hi_Signed), .sel(Sign_Result));
  // Probe on Hi_Signed

  // Other names for the same wires on the sheet: Data_A[31:0] = A; Data_B[31:0] = B;
  //   Selector_Op[1:0] = {A[31], B[31]}; Sign_B = B[31]; Sign_A = A[31]
endmodule

module Signer_Divider (
  input  [31:0] A,
  input  [31:0] B,
  output [31:0] Lo_Div_Sign,
  output [31:0] Remainder_Sign
);

  wire Sign_Result;
  wire [31:0] A_Complement, B_Complement, Lo_A_B, Lo_A_B_Complement, Lo_A_Complement_B,
       Lo_A_Complement_B_Complement, Lo_Complement, Lo_Result, Remainder_A_B, Remainder_A_B_Complement,
       Remainder_A_Complement_B, Remainder_A_Complement_B_Complement, Remainder_Complement, Remainder_Result;

  // Probe on A
  // Probe on B
  xor xor_1 (Sign_Result, A[31], B[31]);
  Divider #(.width(32)) divider_1 (.a(A), .b(B), .out(Lo_A_B), .rem(Remainder_A_B));  // open: upper
  Multiplier #(.width(32)) multiplier_1 (
    .a(A), .b(A_Complement), .out(Lo_A_B_Complement), .cout(Remainder_A_B_Complement));  // open: cin
  Divider #(.width(32)) divider_2 (
    .a(A_Complement), .b(B), .out(Lo_A_Complement_B), .rem(Remainder_A_Complement_B));  // open: upper
  Divider #(.width(32)) divider_3 (
    .a(A_Complement), .b(B_Complement), .out(Lo_A_Complement_B_Complement),
    .rem(Remainder_A_Complement_B_Complement));  // open: upper
  Complemento_A2 complemento_a2_1 (.A(A), .out_2(A_Complement));
  Complemento_A2 complemento_a2_2 (.A(B), .out_2(B_Complement));
  Multiplexer #(.select(2), .width(32), .enable("false")) multiplexer_1 (
    .in0(Lo_A_B), .in1(Lo_A_B_Complement), .in2(Lo_A_Complement_B), .in3(Lo_A_Complement_B_Complement),
    .out(Lo_Result), .sel({A[31], B[31]}));
  Complemento_A2 complemento_a2_3 (.A(Lo_Result), .out_2(Lo_Complement));
  Complemento_A2 complemento_a2_4 (.A(Remainder_Result), .out_2(Remainder_Complement));
  Multiplexer #(.select(2), .width(32), .enable("false")) multiplexer_2 (
    .in0(Remainder_A_B), .in1(Remainder_A_B_Complement), .in2(Remainder_A_Complement_B),
    .in3(Remainder_A_Complement_B_Complement), .out(Remainder_Result), .sel({A[31], B[31]}));
  // Probe on Lo_Div_Sign
  Multiplexer #(.width(32), .enable("false")) multiplexer_3 (
    .in0(Lo_Result), .in1(Lo_Complement), .out(Lo_Div_Sign), .sel(Sign_Result));
  Multiplexer #(.width(32), .enable("false")) multiplexer_4 (
    .in0(Remainder_Result), .in1(Remainder_Complement), .out(Remainder_Sign), .sel(A[31]));
  // Probe on Remainder_Sign

  // Other names for the same wires on the sheet: Data_A[31:0] = A; Select_Op[1:0] = {A[31], B[31]}; Sign_A = A[31];
  //   Data_B[31:0] = B; Sign_B = B[31]
endmodule

module Register_File_2 (
  input  [4:0] DA,
  input  [31:0] DI,
  input  R_W,
  input  [4:0] SA,
  input  [4:0] SB,
  input  Clk,
  input  Reset,
  input  [31:0] Hi,
  input  [31:0] Lo,
  input  R_W_Hi_Lo,
  input  R_W_SP,
  input  Pop,
  output [31:0] Data_A,
  output [31:0] Data_B,
  output [31:0] SP,
  output [31:0] Hi_Out,
  output [31:0] Lo_Out
);

  wire or_1_out, R0, R1, R2, R3, R4, R5, R6, R7, R8, R9, R10, R11, R12, R13, R14, R15, R16, R17, R18, R19,
       R20, R21, R22, R23, R24, R25, R26, R27, R28, R29, R30, R31;
  wire [31:0] adder_1_out, multiplexer_3_out, New_SP, R0_Out, R1_Out, R2_Out, R3_Out, R4_Out, R5_Out, R6_Out,
       R7_Out, R8_Out, R9_Out, R10_Out, R11_Out, R12_Out, R13_Out, R14_Out, R15_Out, R16_Out, R17_Out,
       R18_Out, R19_Out, R20_Out, R21_Out, R22_Out, R23_Out, R24_Out, R25_Out, R26_Out, R27_Out, R28_Out,
       R29_Out, R30_Out, subtractor_1_out;

  Decoder #(.select(5), .disabled(0)) decoder_1 (
    .out0(R0), .out1(R1), .out2(R2), .out3(R3), .out4(R4), .out5(R5), .out6(R6), .out7(R7), .out8(R8),
    .out9(R9), .out10(R10), .out11(R11), .out12(R12), .out13(R13), .out14(R14), .out15(R15), .out16(R16),
    .out17(R17), .out18(R18), .out19(R19), .out20(R20), .out21(R21), .out22(R22), .out23(R23), .out24(R24),
    .out25(R25), .out26(R26), .out27(R27), .out28(R28), .out29(R29), .out30(R30), .out31(R31), .sel(DA),
    .en(R_W));
  Register #(.width(32)) u_R0 (.D({32{1'b0}}), .en(R0), .Q(R0_Out), .clk(Clk), .clr(Reset));
  Register #(.width(32)) u_R4 (.D(DI), .en(R4), .Q(R4_Out), .clk(Clk), .clr(Reset));
  Register #(.width(32)) u_R8 (.D(DI), .en(R8), .Q(R8_Out), .clk(Clk), .clr(Reset));
  Register #(.width(32)) u_R12 (.D(DI), .en(R12), .Q(R12_Out), .clk(Clk), .clr(Reset));
  Register #(.width(32)) u_R16 (.D(DI), .en(R16), .Q(R16_Out), .clk(Clk), .clr(Reset));
  Register #(.width(32)) u_R20 (.D(DI), .en(R20), .Q(R20_Out), .clk(Clk), .clr(Reset));
  Register #(.width(32)) u_R24 (.D(DI), .en(R24), .Q(R24_Out), .clk(Clk), .clr(Reset));
  Register #(.width(32)) u_R28 (.D(DI), .en(R28), .Q(R28_Out), .clk(Clk), .clr(Reset));
  Subtractor #(.width(32)) subtractor_1 (.a(SP), .b(32'h4), .out(subtractor_1_out));  // open: bin, bout
  Adder #(.width(32)) adder_1 (.a(SP), .b(32'h4), .out(adder_1_out));  // open: cin, cout
  Register #(.width(32)) u_R25 (.D(DI), .en(R25), .Q(R25_Out), .clk(Clk), .clr(Reset));
  Register #(.width(32)) u_R29 (.D(DI), .en(R29), .Q(R29_Out), .clk(Clk), .clr(Reset));
  Multiplexer #(.select(5), .width(32), .enable("false")) multiplexer_1 (
    .in0(R0_Out), .in1(R1_Out), .in2(R2_Out), .in3(R3_Out), .in4(R4_Out), .in5(R5_Out), .in6(R6_Out),
    .in7(R7_Out), .in8(R8_Out), .in9(R9_Out), .in10(R10_Out), .in11(R11_Out), .in12(R12_Out), .in13(R13_Out),
    .in14(R14_Out), .in15(R15_Out), .in16(R16_Out), .in17(R17_Out), .in18(R18_Out), .in19(R19_Out),
    .in20(R20_Out), .in21(R21_Out), .in22(R22_Out), .in23(R23_Out), .in24(R24_Out), .in25(R25_Out),
    .in26(R26_Out), .in27(R27_Out), .in28(R28_Out), .in29(R29_Out), .in30(R30_Out), .in31(SP), .out(Data_A),
    .sel(SA));
  Register #(.width(32)) u_R1 (.D(DI), .en(R1), .Q(R1_Out), .clk(Clk), .clr(Reset));
  Register #(.width(32)) u_R5 (.D(DI), .en(R5), .Q(R5_Out), .clk(Clk), .clr(Reset));
  Register #(.width(32)) u_R9 (.D(DI), .en(R9), .Q(R9_Out), .clk(Clk), .clr(Reset));
  Register #(.width(32)) u_R13 (.D(DI), .en(R13), .Q(R13_Out), .clk(Clk), .clr(Reset));
  Register #(.width(32)) u_R17 (.D(DI), .en(R17), .Q(R17_Out), .clk(Clk), .clr(Reset));
  Register #(.width(32)) u_R21 (.D(DI), .en(R21), .Q(R21_Out), .clk(Clk), .clr(Reset));
  Multiplexer #(.width(32), .enable("false")) multiplexer_2 (
    .in0(subtractor_1_out), .in1(adder_1_out), .out(New_SP), .sel(Pop));
  Register #(.width(32)) u_R2 (.D(DI), .en(R2), .Q(R2_Out), .clk(Clk), .clr(Reset));
  Register #(.width(32)) u_R6 (.D(DI), .en(R6), .Q(R6_Out), .clk(Clk), .clr(Reset));
  Register #(.width(32)) u_R10 (.D(DI), .en(R10), .Q(R10_Out), .clk(Clk), .clr(Reset));
  Register #(.width(32)) u_R14 (.D(DI), .en(R14), .Q(R6_Out), .clk(Clk), .clr(Reset));
  Register #(.width(32)) u_R18 (.D(DI), .en(R18), .Q(R18_Out), .clk(Clk), .clr(Reset));
  Register #(.width(32)) u_R22 (.D(DI), .en(R22), .Q(R22_Out), .clk(Clk), .clr(Reset));
  Register #(.width(32)) u_R26 (.D(DI), .en(R26), .Q(R26_Out), .clk(Clk), .clr(Reset));
  Register #(.width(32)) u_R30 (.D(DI), .en(R30), .Q(R30_Out), .clk(Clk), .clr(Reset));
  Multiplexer #(.width(32), .enable("false")) multiplexer_3 (
    .in0(DI), .in1(New_SP), .out(multiplexer_3_out), .sel(R_W_SP));
  or or_1 (or_1_out, R_W_SP, R31);
  Register #(.width(32)) u_R3 (.D(DI), .en(R3), .Q(R3_Out), .clk(Clk), .clr(Reset));
  Register #(.width(32)) u_R7 (.D(DI), .en(R7), .Q(R7_Out), .clk(Clk), .clr(Reset));
  Register #(.width(32)) u_R11 (.D(DI), .en(R11), .Q(R11_Out), .clk(Clk), .clr(Reset));
  Register #(.width(32)) u_R15 (.D(DI), .en(R15), .Q(R15_Out), .clk(Clk), .clr(Reset));
  Register #(.width(32)) u_R19 (.D(DI), .en(R19), .Q(R19_Out), .clk(Clk), .clr(Reset));
  Register #(.width(32)) u_R23 (.D(DI), .en(R23), .Q(R23_Out), .clk(Clk), .clr(Reset));
  Register #(.width(32)) u_R27 (.D(DI), .en(R27), .Q(R27_Out), .clk(Clk), .clr(Reset));
  Multiplexer #(.select(5), .width(32), .enable("false")) multiplexer_4 (
    .in0(R0_Out), .in1(R1_Out), .in2(R2_Out), .in3(R3_Out), .in4(R4_Out), .in5(R5_Out), .in6(R6_Out),
    .in7(R7_Out), .in8(R8_Out), .in9(R9_Out), .in10(R10_Out), .in11(R11_Out), .in12(R12_Out), .in13(R13_Out),
    .in14(R14_Out), .in15(R15_Out), .in16(R16_Out), .in17(R17_Out), .in18(R18_Out), .in19(R19_Out),
    .in20(R20_Out), .in21(R21_Out), .in22(R22_Out), .in23(R23_Out), .in24(R24_Out), .in25(R25_Out),
    .in26(R26_Out), .in27(R27_Out), .in28(R28_Out), .in29(R29_Out), .in30(R30_Out), .in31(SP), .out(Data_B),
    .sel(SB));
  Register #(.width(32)) u_SP (.D(multiplexer_3_out), .en(or_1_out), .Q(SP), .clk(Clk), .clr(Reset));
  Register #(.width(32)) u_Hi (.D(Hi), .en(R_W_Hi_Lo), .Q(Hi_Out), .clk(Clk), .clr(Reset));
  Register #(.width(32)) u_Lo (.D(Lo), .en(R_W_Hi_Lo), .Q(Lo_Out), .clk(Clk), .clr(Reset));

  // Other names for the same wires on the sheet: Rst = Reset; RW = R_W; RWHL = R_W_Hi_Lo; RWSP = R_W_SP;
  //   SP_Out[31:0] = SP

  // Notes on the sheet:
  //   Data Adress
  //   Data In
  //   Read/Write
  //   Selector A
  //   Selector B
  //   Inputs
  //   Write
  //   Registers
  //   Read
  //   Stack Pointer
  //   Outputs
  //   Hi-Lo Registers
endmodule

module Program_Counter_2 (
  input  [31:0] Input,
  input  clk,
  input  Load_PC,
  input  RST,
  output [31:0] Output
);

  Register #(.width(32)) PC (.D(Input), .en(Load_PC), .Q(Output), .clk(clk), .clr(RST));

  // Other names for the same wires on the sheet: LPC = Load_PC; PC_Out[31:0] = Output
endmodule

// 1
module Branch_Control_2 (
  input  [31:0] RS,
  input  [31:0] PC,
  input  [15:0] offset,
  input  [25:0] J_destino,
  input  [2:0] Op_Selector,
  input  RS____RT,
  output [31:0] Output
);

  wire and_1_out, and_2_out, and_3_out, and_4_out, and_5_out, B_jump, beq, bgtz, blez, bltz, bne, j, jr, nop,
       RS___0, RS___0_t, RS____0, RS____0_t;
  wire [1:0] jump;
  wire [31:0] off_jump, PC___4;
  wire [31:18] off;

  Decoder #(.select(3), .enable("false")) decoder_1 (
    .out0(nop), .out1(beq), .out2(bne), .out3(blez), .out4(bgtz), .out5(bltz), .out6(j), .out7(jr),
    .sel(Op_Selector));
  Comparator #(.width(32)) comparator_1 (.a(RS), .b({32{1'b0}}), .gt(RS___0_t), .eq(RS____0_t), .lt(RS___0));
  or or_1 (RS____0, RS____0_t, RS___0);
  Adder #(.width(32)) adder_1 (.a(PC), .b(32'h4), .out(PC___4));  // open: cin, cout
  assign off = {{13{offset[15]}}, offset[15]};  // Bit_Extender bit_extender_1
  and and_1 (and_1_out, beq, RS____RT);
  and and_2 (and_2_out, bne, ~RS____RT);  // AND_Gate
  and and_3 (and_3_out, blez, RS____0);
  and and_4 (and_4_out, bgtz, RS___0_t);
  and and_5 (and_5_out, bltz, RS___0);
  Adder #(.width(32)) adder_2 (.a(PC___4), .b({off, offset, 2'b00}), .out(off_jump));  // open: cin, cout
  Multiplexer #(.select(2), .width(32), .enable("false")) multiplexer_1 (
    .in0(PC___4), .in1(off_jump), .in2(RS), .in3({PC[31:28], J_destino, 2'b00}), .out(Output), .sel(jump));
  or or_2 (B_jump, and_1_out, and_2_out, and_3_out, and_4_out, and_5_out);
  Priority_Encoder #(.select(2)) priority_encoder_1 (
    .in0(1'b1), .in1(B_jump), .in2(j), .in3(jr), .out(jump), .en_in(1'b1));  // open: gs, en_out

  // Other names for the same wires on the sheet: off[17:2] = offset; PC___J[31:2] = {PC[31:28], J_destino};
  //   destino[25:0] = J_destino; selector[2:0] = Op_Selector

  // Notes on the sheet:
  //   Jump Selector
  //   Posible jumps
  //   Big Selector
  //   Output
endmodule

module Instruction_Decoder_2 (
  input  [31:0] Instruction,
  input  LIM,
  input  clk,
  input  RSt,
  output [5:0] Op_Code,
  output [25:0] Destino,
  output [15:0] Constante,
  output [4:0] Rs,
  output [4:0] Rt,
  output [4:0] Rd,
  output [4:0] x,
  output [5:0] Func_Code
);

  Register #(.width(32)) IM (.D(Instruction), .en(LIM), .Q({Op_Code, Destino[25:16], Constante}), .clk(clk), .clr(RSt));

  assign Destino[15:0] = Constante;
  assign Func_Code = Constante[5:0];
  assign Rd = Constante[15:11];
  assign Rs = Destino[25:21];
  assign Rt = Destino[20:16];
  assign x = Constante[10:6];

  // Other names for the same wires on the sheet: Data_In[31:0] = Instruction; Load_IM = LIM
endmodule

module Operation_Decoder (
  input  [5:0] Op_Code,
  input  [5:0] Func_Code,
  output [2:0] CU_Selector,
  output [3:0] Alu_Selector,
  output [2:0] Branch_Selector,
  output [1:0] Special_Selector,
  output pop,
  output lw,
  output Signed_Op,
  output mfhi,
  output Logic_Inm_Op,
  output Mul_Div_Op
);

  wire _000000, _111111, add, addi, Alu_Op, \and , and_23_out, andi, beq, bgtz, blez, bltz, bne, Branch_Op,
       comparator_17_eq, comparator_18_eq, comparator_19_eq, comparator_20_eq, comparator_21_eq,
       comparator_22_eq, comparator_23_eq, comparator_24_eq, comparator_25_eq, comparator_26_eq,
       comparator_27_eq, comparator_28_eq, comparator_29_eq, comparator_30_eq, comparator_31_eq,
       comparator_32_eq, comparator_33_eq, comparator_34_eq, comparator_35_eq, comparator_36_eq,
       comparator_37_eq, comparator_38_eq, comparator_39_eq, comparator_40_eq, div, divu, halt, Inm_Op, j,
       jr, kbd, mflo, mult, mulu, nop, \nor , \or , or_11_out, or_12_out, or_13_out, or_14_out, or_15_out,
       or_16_out, or_17_out, or_18_out, ori, push, Ram_Op, Register_Op, rnd, slt, slti, sltiu, sltu,
       Special_Op, Stack_Op, sub, sw, tty, \xor , xori;

  Comparator #(.width(6)) comparator_1 (.a(Op_Code), .b(6'b001000), .eq(addi));  // open: gt, lt
  Comparator #(.width(6)) comparator_2 (.a(Op_Code), .b(6'b001010), .eq(slti));  // open: gt, lt
  Comparator #(.width(6)) comparator_3 (.a(Op_Code), .b(6'b001011), .eq(sltiu));  // open: gt, lt
  Comparator #(.width(6)) comparator_4 (.a(Op_Code), .b(6'b001100), .eq(andi));  // open: gt, lt
  Comparator #(.width(6)) comparator_5 (.a(Op_Code), .b(6'b001101), .eq(ori));  // open: gt, lt
  Comparator #(.width(6)) comparator_6 (.a(Op_Code), .b(6'b001110), .eq(xori));  // open: gt, lt
  Comparator #(.width(6)) comparator_7 (.a(Op_Code), .b({6{1'b1}}), .eq(_111111));  // open: gt, lt
  Comparator #(.width(6)) comparator_8 (.a(Op_Code), .b({6{1'b0}}), .eq(_000000));  // open: gt, lt
  Comparator #(.width(6)) comparator_9 (.a(Op_Code), .b(6'b100011), .eq(lw));  // open: gt, lt
  Comparator #(.width(6)) comparator_10 (.a(Op_Code), .b(6'b101011), .eq(sw));  // open: gt, lt
  Comparator #(.width(6)) comparator_11 (.a(Op_Code), .b(6'b000100), .eq(beq));  // open: gt, lt
  Comparator #(.width(6)) comparator_12 (.a(Op_Code), .b(6'b000101), .eq(bne));  // open: gt, lt
  Comparator #(.width(6)) comparator_13 (.a(Op_Code), .b(6'b000110), .eq(blez));  // open: gt, lt
  Comparator #(.width(6)) comparator_14 (.a(Op_Code), .b(6'b000111), .eq(bgtz));  // open: gt, lt
  Comparator #(.width(6)) comparator_15 (.a(Op_Code), .b(6'b000001), .eq(bltz));  // open: gt, lt
  Comparator #(.width(6)) comparator_16 (.a(Op_Code), .b(6'b000010), .eq(j));  // open: gt, lt
  Comparator #(.width(6)) comparator_17 (.a(Func_Code), .b({6{1'b0}}), .eq(comparator_17_eq));  // open: gt, lt
  Comparator #(.width(6)) comparator_18 (.a(Func_Code), .b(6'b100000), .eq(comparator_18_eq));  // open: gt, lt
  Comparator #(.width(6)) comparator_19 (.a(Func_Code), .b(6'b100010), .eq(comparator_19_eq));  // open: gt, lt
  Comparator #(.width(6)) comparator_20 (.a(Func_Code), .b(6'b011000), .eq(comparator_20_eq));  // open: gt, lt
  Comparator #(.width(6)) comparator_21 (.a(Func_Code), .b(6'b011001), .eq(comparator_21_eq));  // open: gt, lt
  Comparator #(.width(6)) comparator_22 (.a(Func_Code), .b(6'b011010), .eq(comparator_22_eq));  // open: gt, lt
  Comparator #(.width(6)) comparator_23 (.a(Func_Code), .b(6'b011011), .eq(comparator_23_eq));  // open: gt, lt
  Comparator #(.width(6)) comparator_24 (.a(Func_Code), .b(6'b101010), .eq(comparator_24_eq));  // open: gt, lt
  Comparator #(.width(6)) comparator_25 (.a(Op_Code), .b(6'b111000), .eq(comparator_25_eq));  // open: gt, lt
  Comparator #(.width(6)) comparator_26 (.a(Func_Code), .b({6{1'b0}}), .eq(comparator_26_eq));  // open: gt, lt
  Comparator #(.width(6)) comparator_27 (.a(Op_Code), .b(6'b111000), .eq(comparator_27_eq));  // open: gt, lt
  Comparator #(.width(6)) comparator_28 (.a(Func_Code), .b(6'b000001), .eq(comparator_28_eq));  // open: gt, lt
  and and_1 (nop, _000000, comparator_17_eq);
  and and_2 (add, _000000, comparator_18_eq);
  and and_3 (sub, _000000, comparator_19_eq);
  and and_4 (mult, _000000, comparator_20_eq);
  and and_5 (mulu, _000000, comparator_21_eq);
  and and_6 (div, _000000, comparator_22_eq);
  and and_7 (divu, _000000, comparator_23_eq);
  and and_8 (slt, _000000, comparator_24_eq);
  and and_9 (pop, comparator_25_eq, comparator_26_eq);
  and and_10 (push, comparator_27_eq, comparator_28_eq);
  Comparator #(.width(6)) comparator_29 (.a(Func_Code), .b(6'b101011), .eq(comparator_29_eq));  // open: gt, lt
  Comparator #(.width(6)) comparator_30 (.a(Func_Code), .b(6'b100100), .eq(comparator_30_eq));  // open: gt, lt
  Comparator #(.width(6)) comparator_31 (.a(Func_Code), .b(6'b100101), .eq(comparator_31_eq));  // open: gt, lt
  Comparator #(.width(6)) comparator_32 (.a(Func_Code), .b(6'b100111), .eq(comparator_32_eq));  // open: gt, lt
  Comparator #(.width(6)) comparator_33 (.a(Func_Code), .b(6'b101000), .eq(comparator_33_eq));  // open: gt, lt
  Comparator #(.width(6)) comparator_34 (.a(Func_Code), .b(6'b001000), .eq(comparator_34_eq));  // open: gt, lt
  Comparator #(.width(6)) comparator_35 (.a(Func_Code), .b(6'b010000), .eq(comparator_35_eq));  // open: gt, lt
  Comparator #(.width(6)) comparator_36 (.a(Func_Code), .b(6'b010010), .eq(comparator_36_eq));  // open: gt, lt
  Comparator #(.width(6)) comparator_37 (.a(Func_Code), .b({6{1'b1}}), .eq(comparator_37_eq));  // open: gt, lt
  Comparator #(.width(6)) comparator_38 (.a(Func_Code), .b(6'b000001), .eq(comparator_38_eq));  // open: gt, lt
  Comparator #(.width(6)) comparator_39 (.a(Func_Code), .b(6'b000010), .eq(comparator_39_eq));  // open: gt, lt
  Comparator #(.width(6)) comparator_40 (.a(Func_Code), .b(6'b000100), .eq(comparator_40_eq));  // open: gt, lt
  and and_11 (sltu, _000000, comparator_29_eq);
  and and_12 (\and , _000000, comparator_30_eq);
  and and_13 (\or , _000000, comparator_31_eq);
  and and_14 (\nor , _000000, comparator_32_eq);
  and and_15 (\xor , _000000, comparator_33_eq);
  and and_16 (jr, _000000, comparator_34_eq);
  and and_17 (mfhi, _000000, comparator_35_eq);
  and and_18 (mflo, _000000, comparator_36_eq);
  and and_19 (halt, _111111, comparator_37_eq);
  and and_20 (tty, _111111, comparator_38_eq);
  and and_21 (rnd, _111111, comparator_39_eq);
  and and_22 (kbd, _111111, comparator_40_eq);
  or or_1 (Branch_Op, nop, beq, bne, blez, bgtz, bltz, j, jr);
  or or_2 (Inm_Op, addi, slti, sltiu, andi, ori, xori);
  or or_3 (Logic_Inm_Op, andi, ori, xori);
  or or_4 (Special_Op, halt, rnd, kbd, tty);
  or or_5 (Stack_Op, pop, push);
  or or_6 (Ram_Op, lw, sw);
  or or_7 (Register_Op, mfhi, mflo);
  or or_8 (Mul_Div_Op, mult, mulu, div, divu);
  or or_9 (Signed_Op, mult, div);
  or or_10 (Alu_Op, add, sub, mult, mulu, div, divu, slt, sltu, \and , \or , \nor , \xor );
  or or_11 (or_11_out, add, addi);
  or or_12 (or_12_out, \and , andi);
  or or_13 (or_13_out, \or , ori);
  or or_14 (or_14_out, \xor , xori);
  or or_15 (or_15_out, slt, slti);
  or or_16 (or_16_out, sltu, sltiu);
  and and_23 (and_23_out, ~Alu_Op, ~Inm_Op);  // AND_Gate
  or or_17 (or_17_out, nop, 1'b1);
  or or_18 (or_18_out, halt, 1'b1);
  Priority_Encoder priority_encoder_1 (
    .in0(Branch_Op), .in1(Alu_Op), .in2(Inm_Op), .in3(Register_Op), .in4(Ram_Op), .in5(Stack_Op),
    .in6(Special_Op), .out(CU_Selector), .en_in(1'b1));  // open: in7, gs, en_out
  Priority_Encoder #(.select(2)) priority_encoder_2 (
    .in0(or_18_out), .in1(rnd), .in2(kbd), .in3(tty), .out(Special_Selector), .en_in(1'b1));  // open: gs, en_out
  Priority_Encoder #(.select(4)) priority_encoder_3 (
    .in0(or_11_out), .in1(sub), .in2(mult), .in3(mulu), .in4(div), .in5(divu), .in6(or_12_out),
    .in7(or_13_out), .in8(\nor ), .in9(or_14_out), .in10(or_15_out), .in11(or_16_out), .in15(and_23_out),
    .out(Alu_Selector), .en_in(1'b1));  // open: in12, in13, in14, gs, en_out
  Priority_Encoder priority_encoder_4 (
    .in0(or_17_out), .in1(beq), .in2(bne), .in3(blez), .in4(bgtz), .in5(bltz), .in6(j), .in7(jr),
    .out(Branch_Selector), .en_in(1'b1));  // open: gs, en_out

  // Notes on the sheet:
  //   Tipo I
  //   Tipo J
  //   Tipo R
endmodule

module Next_Adress (
  input  [31:0] PC,
  input  [15:0] Constant,
  input  [31:0] Rs,
  input  [31:0] SP,
  input  Stack__Op,
  input  RAM_Op,
  output [15:0] Adress,
  output [1:0] offset,
  output [3:0] Mask
);

  wire [31:0] bit_extender_1_out, multiplexer_1_out, Rs___Constant;

  assign bit_extender_1_out = {{16{Constant[15]}}, Constant};  // Bit_Extender bit_extender_1
  Multiplexer #(.select(2), .width(32), .enable("false")) multiplexer_1 (
    .in0(PC), .in1(SP), .in2(Rs___Constant),
    .out({multiplexer_1_out[31:20], Adress, offset, multiplexer_1_out[1:0]}), .sel({RAM_Op, Stack__Op}));  // open: in3
  Adder #(.width(32)) adder_1 (.a(Rs), .b(bit_extender_1_out), .out(Rs___Constant));  // open: cin, cout
  Demultiplexer #(.select(2), .enable("false")) demultiplexer_1 (
    .out0(Mask[0]), .out1(Mask[1]), .out2(Mask[2]), .out3(Mask[3]), .in(1'b1), .sel(offset));

  // Other names for the same wires on the sheet: Stack_Op = Stack__Op
endmodule

module Little_Endian (
  input  [31:0] in_1,
  output [31:0] Output
);


  assign Output = {in_1[7:0], in_1[15:8], in_1[23:16], in_1[31:24]};
endmodule

module DataPath (
  input  [31:0] Bank_0,
  input  [31:0] Bank_1,
  input  [31:0] Bank_2,
  input  [31:0] Bank_3,
  input  [31:0] KBD_Data,
  input  [3:0] Alu_Op,
  input  [2:0] Branch_Op,
  input  Clk,
  input  Reset,
  input  Load_PC,
  input  Load_Inst,
  input  R___W,
  input  Inme_Op,
  input  Logical_Inme_Op,
  input  Hi_Lo_Register_Op,
  input  mfhi,
  input  Ram_Op,
  input  lw,
  input  Stack_Op,
  input  pop,
  input  Load_SP,
  input  Hi_Selector,
  input  Signed_Op,
  input  KBD,
  input  Random,
  output [31:0] To_Ram,
  output [15:0] Adress,
  output [5:0] Op_Code,
  output [5:0] Func_Code,
  output [6:0] tty,
  output [1:0] offset,
  output [3:0] Mask
);

  wire and_1_out, Negative, or_1_out, Rs____Rt, Rs___Rt, Rs___Rt_t, Zero;
  wire [4:0] multiplexer_4_out, Rd, Rs, Rt, x;
  wire [15:0] Constant;
  wire [25:0] Destiny;
  wire [31:0] bit_extender_1_out, bit_extender_2_out, High, Instruction, Low, multiplexer_1_out,
       multiplexer_2_out, multiplexer_3_out, multiplexer_5_out, multiplexer_6_out, multiplexer_7_out,
       multiplexer_8_out, multiplexer_9_out, multiplexer_11_out, New_Direction, PC, random_1_out,
       Register_Data, Register_High, Register_Low, Register_Rt, Register_SP;
  wire [31:7] Register_RS;

  Program_Counter_2 program_counter_1 (.Input(PC), .clk(Clk), .Load_PC(Load_PC), .RST(Reset), .Output(New_Direction));
  Multiplexer #(.select(2), .width(32), .enable("false")) multiplexer_1 (
    .in0(Bank_0), .in1(Bank_1), .in2(Bank_2), .in3(Bank_3), .out(multiplexer_1_out), .sel(offset));
  Next_Adress next_adress_1 (
    .PC(New_Direction), .Constant(Constant), .Rs({Register_RS, tty}), .SP(Register_SP), .Stack__Op(Stack_Op),
    .RAM_Op(Ram_Op), .Adress(Adress), .offset(offset), .Mask(Mask));
  Branch_Control_2 branch_control_1 (
    .RS({Register_RS, tty}), .PC(New_Direction), .offset(Constant), .J_destino(Destiny),
    .Op_Selector(Branch_Op), .RS____RT(Rs____Rt), .Output(PC));
  Little_Endian little_endian_1 (.in_1(multiplexer_1_out), .Output(Instruction));
  Instruction_Decoder_2 instruction_decoder_1 (
    .Instruction(Instruction), .LIM(Load_Inst), .clk(Clk), .RSt(Reset), .Op_Code(Op_Code), .Destino(Destiny),
    .Constante(Constant), .Rs(Rs), .Rt(Rt), .Rd(Rd), .x(x), .Func_Code(Func_Code));
  assign bit_extender_1_out = {{16{Constant[15]}}, Constant};  // Bit_Extender bit_extender_1
  assign bit_extender_2_out = {{16{1'b0}}, Constant};  // Bit_Extender bit_extender_2
  Multiplexer #(.width(32), .enable("false")) multiplexer_2 (
    .in0(bit_extender_1_out), .in1(bit_extender_2_out), .out(multiplexer_2_out), .sel(Logical_Inme_Op));
  Multiplexer #(.width(32), .enable("false")) multiplexer_3 (
    .in0(Register_Low), .in1(Register_High), .out(multiplexer_3_out), .sel(mfhi));
  or or_1 (or_1_out, Inme_Op, Ram_Op);
  Multiplexer #(.width(5), .enable("false")) multiplexer_4 (
    .in0(Rd), .in1(Rt), .out(multiplexer_4_out), .sel(or_1_out));
  and and_1 (and_1_out, R___W, ~Hi_Selector);  // AND_Gate
  Multiplexer #(.width(32), .enable("false")) multiplexer_5 (
    .in0(Register_Rt), .in1(multiplexer_2_out), .out(multiplexer_5_out), .sel(Inme_Op));
  Multiplexer #(.width(32), .enable("false")) multiplexer_6 (
    .in0(Low), .in1(multiplexer_3_out), .out(multiplexer_6_out), .sel(Hi_Lo_Register_Op));
  Multiplexer #(.width(32), .enable("false")) multiplexer_7 (
    .in0(multiplexer_6_out), .in1(Instruction), .out(multiplexer_7_out), .sel(lw));
  Multiplexer #(.width(32), .enable("false")) multiplexer_8 (
    .in0(multiplexer_7_out), .in1(Instruction), .out(multiplexer_8_out), .sel(pop));
  ALU_2 alu_1 (
    .Rs({Register_RS, tty}), .Rt(multiplexer_5_out), .in_3(Alu_Op), .Cero(Zero), .Negative(Negative),
    .Output__Lo(Low), .Hi(High), .Hi_Selector(Hi_Selector), .Signed_Op(Signed_Op), .Less(Rs___Rt),
    .Equal(Rs____Rt), .Great(Rs___Rt_t));
  Multiplexer #(.width(32), .enable("false")) multiplexer_9 (
    .in0(multiplexer_8_out), .in1(KBD_Data), .out(multiplexer_9_out), .sel(KBD));
  Register_File_2 register_file_1 (
    .DA(multiplexer_4_out), .DI(Register_Data), .R_W(and_1_out), .SA(Rs), .SB(Rt), .Clk(Clk), .Reset(Reset),
    .Data_A({Register_RS, tty}), .Data_B(Register_Rt), .SP(Register_SP), .Hi(High), .Lo(Low),
    .R_W_Hi_Lo(Hi_Selector), .Hi_Out(Register_High), .Lo_Out(Register_Low), .R_W_SP(Load_SP), .Pop(pop));
  Multiplexer #(.width(32), .enable("false")) multiplexer_10 (
    .in0(multiplexer_9_out), .in1(random_1_out), .out(Register_Data), .sel(Random));
  Random #(.width(32)) random_1 (.clk(Clk), .out(random_1_out));  // open: next, clr
  Multiplexer #(.width(32), .enable("false")) multiplexer_11 (
    .in0(Register_Rt), .in1({Register_RS, tty}), .out(multiplexer_11_out), .sel(Stack_Op));
  Little_Endian little_endian_2 (.in_1(multiplexer_11_out), .Output(To_Ram));

  // Other names for the same wires on the sheet: R___W_RF = R___W; Register_RS[6:0] = tty; RST = Reset
endmodule

module Control_Unit_2 (
  input  [5:0] Op_code,
  input  [5:0] Func_code,
  input  [3:0] Read_Time,
  input  [3:0] Write_Time,
  input  Clk,
  input  Reset,
  output [3:0] Alu,
  output [2:0] Branch,
  output Sign,
  output MFHI,
  output Logic,
  output Mul_Div,
  output Inmediate,
  output Hi_Lo,
  output Output,
  output KBD_DP,
  output S_lw,
  output Stack_Op,
  output S_pop,
  output SP,
  output KBD_Enable,
  output TTY_Enable,
  output CS,
  output R_W_RAM,
  output Load_PC,
  output Load_Inst,
  output R_W,
  output RAM_Op,
  output End_Program
);

  wire CS_0, CS_1, CS_2, CS_3, CS_4, d_ff_1_q, d_ff_2_q, d_ff_4_q, d_ff_9_q, d_ff_10_q, d_ff_12_q,
       demultiplexer_1_out0, demultiplexer_1_out1, demultiplexer_2_out0, demultiplexer_3_out0,
       demultiplexer_3_out4, demultiplexer_3_out5, demultiplexer_3_out6, demultiplexer_4_out0,
       demultiplexer_4_out1, demultiplexer_5_out1, demultiplexer_6_out0, demultiplexer_7_out0,
       demultiplexer_7_out1, demultiplexer_8_out0, demultiplexer_9_out0, demultiplexer_9_out1,
       demultiplexer_10_out0, demultiplexer_11_out0, LW_Op, nor_1_out, not_1_out, or_1_out, or_2_out,
       or_3_out, or_4_out, or_5_out, or_6_out, POP_Op, R_W_1, SP_1, \wait ;
  wire [1:0] SP_Op;
  wire [2:0] CU_Op;
  wire [3:0] counter_1_q, RT____WT;

  Multiplexer #(.width(4), .enable("false")) multiplexer_1 (
    .in0(Read_Time), .in1(Write_Time), .out(RT____WT), .sel(R_W_RAM));
  D_Flip_Flop #(.trigger("falling")) d_ff_1 (.clk(Clk), .D(CS), .Q(d_ff_1_q), .reset(Reset));  // open: Qn, preset, en
  Counter #(.width(4), .max('hf)) counter_1 (
    .load(CS), .D(RT____WT), .count(d_ff_1_q), .Q(counter_1_q), .clk(Clk));  // open: carry, clr
  Operation_Decoder operation_decoder_1 (
    .Op_Code(Op_code), .Func_Code(Func_code), .CU_Selector(CU_Op), .Alu_Selector(Alu),
    .Branch_Selector(Branch), .Special_Selector(SP_Op), .pop(POP_Op), .lw(LW_Op), .Signed_Op(Sign),
    .mfhi(MFHI), .Logic_Inm_Op(Logic), .Mul_Div_Op(Mul_Div));
  nor nor_1 (nor_1_out, counter_1_q[0], counter_1_q[1], counter_1_q[2], counter_1_q[3]);
  and and_1 (\wait , nor_1_out, d_ff_1_q);
  D_Flip_Flop #(.trigger("falling")) d_ff_2 (
    .clk(Clk), .D(demultiplexer_1_out0), .Q(d_ff_2_q), .preset(Reset));  // open: Qn, en, reset
  Demultiplexer #(.enable("false")) demultiplexer_1 (
    .out0(demultiplexer_1_out0), .out1(demultiplexer_1_out1), .in(d_ff_2_q), .sel(not_1_out));
  not not_1 (not_1_out, Reset);
  or or_1 (or_1_out, demultiplexer_2_out0, d_ff_12_q, demultiplexer_1_out1);
  D_Flip_Flop #(.trigger("falling")) d_ff_3 (.clk(Clk), .D(or_1_out), .Q(CS_0), .reset(Reset));  // open: Qn, preset, en
  Demultiplexer #(.enable("false")) demultiplexer_2 (
    .out0(demultiplexer_2_out0), .out1(Load_Inst), .in(CS_0), .sel(\wait ));
  D_Flip_Flop #(.trigger("falling")) d_ff_4 (
    .clk(Clk), .D(Load_Inst), .Q(d_ff_4_q), .reset(Reset));  // open: Qn, preset, en
  Demultiplexer #(.select(3), .enable("false")) demultiplexer_3 (
    .out0(demultiplexer_3_out0), .out1(R_W_1), .out2(Inmediate), .out3(Hi_Lo), .out4(demultiplexer_3_out4),
    .out5(demultiplexer_3_out5), .out6(demultiplexer_3_out6), .in(d_ff_4_q), .sel(CU_Op));  // open: out7
  Demultiplexer #(.enable("false")) demultiplexer_4 (
    .out0(demultiplexer_4_out0), .out1(demultiplexer_4_out1), .in(demultiplexer_3_out4), .sel(LW_Op));
  Demultiplexer #(.enable("false")) demultiplexer_5 (
    .out0(SP_1), .out1(demultiplexer_5_out1), .in(demultiplexer_3_out5), .sel(POP_Op));
  Demultiplexer #(.select(2), .enable("false")) demultiplexer_6 (
    .out0(demultiplexer_6_out0), .out1(Output), .out2(KBD_DP), .out3(TTY_Enable), .in(demultiplexer_3_out6),
    .sel(SP_Op));
  or or_2 (or_2_out, demultiplexer_7_out0, demultiplexer_4_out0);
  or or_3 (or_3_out, demultiplexer_9_out0, SP_1);
  or or_4 (or_4_out, demultiplexer_11_out0, demultiplexer_5_out1);
  D_Flip_Flop #(.trigger("falling")) d_ff_5 (.clk(Clk), .D(or_2_out), .Q(CS_1), .reset(Reset));  // open: Qn, preset, en
  D_Flip_Flop #(.trigger("falling")) d_ff_6 (.clk(Clk), .D(or_5_out), .Q(CS_2), .reset(Reset));  // open: Qn, preset, en
  or or_5 (or_5_out, demultiplexer_8_out0, demultiplexer_4_out1);
  D_Flip_Flop #(.trigger("falling")) d_ff_7 (.clk(Clk), .D(or_3_out), .Q(CS_3), .reset(Reset));  // open: Qn, preset, en
  D_Flip_Flop #(.trigger("falling")) d_ff_8 (.clk(Clk), .D(or_4_out), .Q(CS_4), .reset(Reset));  // open: Qn, preset, en
  D_Flip_Flop #(.trigger("falling")) d_ff_9 (
    .clk(Clk), .D(TTY_Enable), .Q(d_ff_9_q), .reset(Reset));  // open: Qn, preset, en
  Demultiplexer #(.enable("false")) demultiplexer_7 (
    .out0(demultiplexer_7_out0), .out1(demultiplexer_7_out1), .in(CS_1), .sel(\wait ));
  Demultiplexer #(.enable("false")) demultiplexer_8 (.out0(demultiplexer_8_out0), .out1(S_lw), .in(CS_2), .sel(\wait ));
  or or_6 (or_6_out, demultiplexer_10_out0, demultiplexer_6_out0);
  Demultiplexer #(.enable("false")) demultiplexer_9 (
    .out0(demultiplexer_9_out0), .out1(demultiplexer_9_out1), .in(CS_3), .sel(\wait ));
  D_Flip_Flop #(.trigger("falling")) d_ff_10 (
    .clk(Clk), .D(or_6_out), .Q(d_ff_10_q), .reset(Reset));  // open: Qn, preset, en
  Demultiplexer #(.enable("false")) demultiplexer_10 (
    .out0(demultiplexer_10_out0), .out1(End_Program), .in(d_ff_10_q), .sel(\wait ));
  D_Flip_Flop #(.trigger("falling")) d_ff_11 (
    .clk(Clk), .D(KBD_DP), .Q(KBD_Enable), .reset(Reset));  // open: Qn, preset, en
  Demultiplexer #(.enable("false")) demultiplexer_11 (
    .out0(demultiplexer_11_out0), .out1(S_pop), .in(CS_4), .sel(\wait ));
  or or_7 (Load_PC, demultiplexer_3_out0, R_W_1, Inmediate, Hi_Lo, demultiplexer_7_out1, S_lw, demultiplexer_9_out1, S_pop, Output, KBD_Enable, d_ff_9_q);
  D_Flip_Flop #(.trigger("falling")) d_ff_12 (
    .clk(Clk), .D(Load_PC), .Q(d_ff_12_q), .reset(Reset));  // open: Qn, preset, en
  or or_8 (RAM_Op, CS_1, CS_2);
  or or_9 (R_W_RAM, CS_1, CS_3);
  or or_10 (Stack_Op, CS_3, CS_4);
  or or_11 (SP, SP_1, S_pop);
  or or_12 (CS, CS_1, CS_2, CS_3, CS_4);
  or or_13 (R_W, R_W_1, Inmediate, Hi_Lo, S_lw, S_pop, Output, KBD_DP);

  // Other names for the same wires on the sheet: ALU_Op[3:0] = Alu; Branch_Op[2:0] = Branch; Logic_Op = Logic;
  //   MFHI_Op = MFHI; Mul_Div_Op = Mul_Div; R_W_2 = Inmediate; R_W_3 = Hi_Lo; R_W_4 = S_lw; R_W_7 = KBD_DP;
  //   R_W_Ram_1 = CS_1; Ram_Op_1 = CS_1; Ram_Op_2 = CS_2; R_W_6 = Output; Rand = Output; RT[3:0] = Read_Time;
  //   Sign_Op = Sign; R_W_5 = S_pop; SP_2 = S_pop; R_W_Ram_2 = CS_3; Stack_Op_1 = CS_3; Stack_Op_2 = CS_4;
  //   WT[3:0] = Write_Time

  // Notes on the sheet:
  //   Stack
  //   Special
  //   Branch
  //   ALU
  //   Inm
  //   Ram
  //   Register
  //   save
  //   push
  //   pop
  //   load
endmodule
